# Fritzing sketch ispled (saved by Fritzing 0.9.3b)
circuit board: 4.70789cm x 2.89023cm
breadboards: 1

parts:
  Q3 = NPN-Transistor [package="TO92 [THT]"]
  R1 = Resistor [tolerance=±5% resistance=200 package=THT]
  R2 = Resistor [tolerance=±5% resistance=120 package=THT]
  R3 = Resistor [tolerance=±5% resistance=120 package=THT]
  LED1 = RGB LED - (4 legs) [current=20 package="5 mm [THT]"]
  Q4 = NPN-Transistor [package="TO92 [THT]"]
  Q5 = NPN-Transistor [package="TO92 [THT]"]
  R4 = Resistor [tolerance=±5% resistance=1k package=THT]
  R5 = Resistor [tolerance=±5% resistance=1k package=THT]
  R6 = Resistor [tolerance=±5% resistance=1k package=THT]
  J1 = female pin header, 5 pins [form="♀ (female)"]

nets:
  GND: Q3.E, Q4.E, Q5.E, J1.pin1
  N1: Q3.B, R4.Pin_1
  N2: Q3.C, R1.Pin_0
  N3: R1.Pin_1, LED1.red_cathode
  N4: R2.Pin_0, Q4.C
  N5: R2.Pin_1, LED1.green_cathode
  N6: R3.Pin_0, Q5.C
  N7: R3.Pin_1, LED1.blue_cathode
  5V: LED1.common_anode, J1.pin5
  N8: Q4.B, R5.Pin_1
  N9: Q5.B, R6.Pin_1
  N10: R4.Pin_0, J1.pin4
  N11: R5.Pin_0, J1.pin3
  N12: R6.Pin_0, J1.pin2

notes:
  ESL-V50RGBC010-CA
  Common anode
  B G A R
  1 2 3 4 min typ max Rtyp5V
  R 1.8V 2.0V 2.2V 200
  VF IF=20mA G 3.0V 3.2V 3.4V 120
  B 3.0V 3.2V 3.4V 120
