# Fritzing sketch modbustestslavehat (saved by Fritzing 0.9.3b)
circuit board: 5.49986cm x 5.4613cm
perfboards: 1

parts:
  U1 = MAX485 [package=dil08]
  JP1 = Header 4 [package=screwterminal-3.5mm-4_lock]
  Part1 = gos_fixed_oled_128x32 [part_number=931]
  LED1 = LED - 5mm [color="Blue (505nm)" package="5 mm [THT]"]
  LED3 = LED - 5mm [color="Red (633nm)" package="5 mm [THT]"]
  LED4 = LED - 5mm [color="Red (633nm)" package="5 mm [THT]"]
  R3 = Resistor [tolerance=±5% resistance=220 package=THT]
  R5 = Resistor [tolerance=±5% resistance=330 package=THT]
  R6 = Resistor [tolerance=±5% resistance=330 package=THT]
  R7 = Resistor [tolerance=±5% resistance=220 package=THT]
  R13 = Trimmer Potentiometer [maximum_resistance=10kΩ package=THT]
  R14 = Trimmer Potentiometer [maximum_resistance=10kΩ package=THT]
  S1 = Pushbutton [package="[THT]"]
  S2 = Pushbutton [package="[THT]"]
  R2 = Resistor [tolerance=±5% resistance=12k package=THT]
  R11 = Resistor [tolerance=±5% resistance=150 package=THT]
  R9 = Resistor [tolerance=±5% resistance=150 package=THT]
  LED2 = LED - 5mm [color="Blue (505nm)" package="5 mm [THT]"]
  LED5 = LED - 5mm [color="Yellow (585nm)" package="5 mm [THT]"]
  LED6 = LED - 5mm [color="Green (560nm)" package="5 mm [THT]"]
  Part2 = Arduino Uno (Rev3)

nets:
  N1: U1.RO, Part2.D0/RX
  N2: U1.RE, U1.DE, R2.Pin_0, Part2.D2
  N3: U1.DI, Part2.D1/TX
  GND: U1.GND, JP1.4, Part1.connector5, R3.Pin_1, R5.Pin_1, R6.Pin_1, R7.Pin_1, R13.leg1, R14.leg1, S1.Pin_1, S1.Pin_2, S2.Pin_1, S2.Pin_2, R2.Pin_1, R11.Pin_1, R9.Pin_1, Part2.GND
  N4: U1.A, JP1.3
  N5: U1.B, JP1.2
  5V: U1.VCC, JP1.1, Part1.connector6, R13.leg2, R14.leg2, Part2.5V
  N6: LED1.cathode, R11.Pin_0
  N7: LED1.anode, Part2.D6_PWM
  N8: LED3.cathode, R3.Pin_0
  N9: LED3.anode, Part2.D11_PWM/MOSI
  N10: LED4.cathode, R7.Pin_0
  N11: LED4.anode, Part2.D3_PWM
  N12: R5.Pin_0, LED5.cathode
  N13: R6.Pin_0, LED6.cathode
  N14: R13.wiper, Part2.A0
  N15: R14.wiper, Part2.A1
  N16: S1.Pin_3, S1.Pin_4, Part2.D7
  N17: S2.Pin_3, S2.Pin_4, Part2.D4
  N18: R9.Pin_0, LED2.cathode
  N19: LED2.anode, Part2.D5_PWM
  N20: LED5.anode, Part2.D10_PWM/SS
  N21: LED6.anode, Part2.D9_PWM
