# Fritzing sketch modbusslwithrs485mixed (saved by Fritzing 0.9.3b)
perfboards: 1

parts:
  Arduino1 = Arduino Pro Mini (5V)
  U1 = MAX485 [package=dil08]
  JP1 = Header 4 [package=screwterminal-3.5mm-4_lock]
  Part1 = gos_fixed_oled_128x32 [part_number=931]
  LED1 = LED - 5mm [color="Blue (505nm)" package="5 mm [THT]"]
  LED2 = LED - 5mm [color="Blue (505nm)" package="5 mm [THT]"]
  LED3 = LED - 5mm [color="Yellow (585nm)" package="5 mm [THT]"]
  LED4 = LED - 5mm [color="Green (555nm)" package="5 mm [THT]"]
  IC1 = Voltage Regulator [package=78xxl]
  C1 = Electrolytic Capacitor [capacitance=1µF package="100 mil [THT, electrolytic]"]
  C2 = Electrolytic Capacitor [capacitance=1µF package="100 mil [THT, electrolytic]"]
  LED5 = DUO LED RG [package="5 mm [THT]"]
  J1 = Power Jack [package=power_jack_pth]
  Q1 = NPN-Transistor [package="TO92 [THT]"]
  R3 = Resistor [tolerance=±5% resistance=220 package=THT]
  R4 = Resistor [tolerance=±5% resistance=10k package=THT]
  R5 = Resistor [tolerance=±5% resistance=220 package=THT]
  R6 = Resistor [tolerance=±5% resistance=220 package=THT]
  R7 = Resistor [tolerance=±5% resistance=220 package=THT]
  R8 = Resistor [tolerance=±5% resistance=10k package=THT]
  R9 = Resistor [tolerance=±5% resistance=220 package=THT]
  Q3 = NPN-Transistor [package="TO92 [THT]"]
  R10 = Resistor [tolerance=±5% resistance=10k package=THT]
  R11 = Resistor [tolerance=±5% resistance=220 package=THT]
  Q4 = NPN-Transistor [package="TO92 [THT]"]
  R12 = Resistor [tolerance=±5% resistance=10k package=THT]
  R13 = Trimmer Potentiometer [maximum_resistance=10kΩ package=THT]  # not connected
  R14 = Trimmer Potentiometer [maximum_resistance=10kΩ package=THT]  # not connected
  S1 = Pushbutton [package="[THT]"]
  S2 = Pushbutton [package="[THT]"]
  Q2 = NPN-Transistor [package="TO92 [THT]"]
  R2 = Resistor [tolerance=±5% resistance=12k package=THT]

nets:
  5V: Arduino1.VCC, U1.VCC, JP1.1, LED1.anode, LED2.anode, LED3.anode, LED4.anode, IC1.OUT, C1.+
  GND: Arduino1.GND, U1.GND, JP1.4, Part1.connector5, IC1.GND, C1.-, C2.-, J1.GND, Q1.E, Q3.E, Q4.E, Q2.E, R2.Pin_1
  N1: Arduino1.A4, Part1.connector8
  N2: Arduino1.A5, Part1.connector7
  N3: Arduino1.D10, R4.Pin_0
  N4: Arduino1.D9, R8.Pin_0
  N5: Arduino1.D6, R5.Pin_1
  N6: Arduino1.D5, R6.Pin_0
  N7: Arduino1.D3, R12.Pin_1
  N8: Arduino1.D2, U1.RE, U1.DE, R2.Pin_0
  N9: Arduino1.RXI, U1.RO
  N10: Arduino1.TXO, U1.DI
  N11: U1.A, JP1.3
  N12: U1.B, JP1.2
  N13: LED1.cathode, R11.Pin_0
  N14: LED2.cathode, R9.Pin_0
  N15: LED3.cathode, R3.Pin_0
  N16: LED4.cathode, R7.Pin_0
  12V: IC1.IN, C2.+, J1.PWR
  N17: LED5.red_anode, R5.Pin_0
  N18: LED5.green_anode, R6.Pin_1
  N19: Q1.B, R4.Pin_1
  N20: Q1.C, R3.Pin_1
  N21: R7.Pin_1, Q2.C
  N22: R8.Pin_1, Q2.B
  N23: R9.Pin_1, Q3.C
  N24: Q3.B, R10.Pin_1
  N25: R11.Pin_1, Q4.C
  N26: Q4.B, R12.Pin_0
  N27: S1.Pin_1, S1.Pin_2
  N28: S1.Pin_3, S1.Pin_4
  N29: S2.Pin_1, S2.Pin_2
  N30: S2.Pin_3, S2.Pin_4
