# Fritzing sketch rs485usbpromicro2 (saved by Fritzing 0.9.3b)
circuit board: 5.86463cm x 3.78816cm
breadboards: 1

parts:
  R1 = Resistor [tolerance=±5% resistance=150 package=THT]
  R2 = Resistor [tolerance=±5% resistance=220 package=THT]
  LED1 = LED - 5mm [color="Yellow (585nm)" package="5 mm [THT]"]
  LED2 = LED - 5mm [color="Green (555nm)" package="5 mm [THT]"]
  J1 = screw terminal, 4 pins
  U1 = MAX485 [package=dil08]
  C1 = Tantalum Capacitor [capacitance=0.1µF package="100 mil [THT, tantalum]"]
  R3 = Resistor [tolerance=±5% resistance=10k package=THT]
  R4 = Resistor [tolerance=±5% resistance=10k package=THT]
  R5 = Resistor [tolerance=±5% resistance=10k package=THT]
  Pro_Micro1 = SparkFun Pro Micro

nets:
  GND: R1.Pin_0, R2.Pin_0, J1.pin4, U1.GND, C1.-, Pro_Micro1.GND
  N1: R1.Pin_1, LED1.cathode
  N2: R2.Pin_1, LED2.cathode
  N3: LED2.anode, Pro_Micro1.6
  5V: J1.pin1, U1.VCC, C1.+, R3.Pin_0, R4.Pin_0, R5.Pin_0, Pro_Micro1.VCC
  N4: J1.pin2, U1.B
  N5: J1.pin3, U1.A
  N6: U1.RO, R5.Pin_1, Pro_Micro1.10
  N7: U1.RE, U1.DE, R3.Pin_1, Pro_Micro1.8
  N8: U1.DI, R4.Pin_1, Pro_Micro1.9

custom parts:
  SparkFun Pro Micro: The Pro Micro is similar to the Pro Mini except with an ATmega32U4 on board. The USB transceiver inside the 32U4 allows us to add USB connectivity on-board and do away with bulky external USB interface. Based on: https://github.com/unorthodox-engineers/unorthodox-arduino/blob/master/Unorthodox/fritzing/parts/Pro%20Micro.fzpz

// code stored in the sketch: rs485usbpromicro.ino
/*
 * Name:    rs485usb.ino
 * Created: 7/14/2019 2:23:09 AM
 * Author:  SigurdssonGO
 * 
 * Software Serial Limitations
 * 
 * The RX pin must support change interrupt
 * On the Mega and Mega 2560 support the following can be used for RX: 10, 11, 12, 13, 14, 15, 50, 51, 52, 53, A8 (62), A9 (63), A10 (64), A11 (65), A12 (66), A13 (67), A14 (68), A15 (69).
 * On the Leonardo and Micro the following can be used for RX: 8, 9, 10, 11, 14 (MISO), 15 (SCK), 16 (MOSI)
 * 
 * On Arduino or Genuino 101 the current maximum RX speed is 57600bps
 * On Arduino or Genuino 101 RX doesn't work on Pin 13
 * 
 */


#include <SoftwareSerial.h>
#include <MAX485.h>


// 4->RE (MAX485 PIN 2), 7->DE (MAX485 PIN 3)
/* Driver Enable set to HIGH to enable transmitting */
//#define PIN_RS485_RE    8
/* Receiver Enable set to LOW to enable receive */
//#define PIN_RS485_DE    9


// Same pin for RE and DE 7->RE (MAX485 PIN 2), 7->DE (MAX485 PIN 3)
#define PIN_RS485_TE    8



// RX(10)->RO (MAX845 PIN 1), TX(11)->DI (MAX845 PIN 4)
#define PIN_SOFT_RX_RO  10
#define PIN_SOFT_TX_DI  11


#define PIN_INDICATOR_LED_DIRECTION_A 5
#define PIN_INDICATOR_LED_DIRECTION_B 6


#define BAUD_RATE     9600


#define SEND_ALL_BUFFERED


SoftwareSerial softser(PIN_SOFT_RX_RO, PIN_SOFT_TX_DI);


#if (defined(PIN_RS485_RE) && defined(PIN_RS485_DE)) || defined(PIN_RS485_TE)
#define USING_MAX_485
#define RS485_MASTER
// Setup max485 Control Input
#ifdef PIN_RS485_TE
MAX485 max485(PIN_RS485_TE);
#else
MAX485 max485(PIN_RS485_RE, PIN_RS485_DE);
#endif
bool issending = false, isreceiving = false;
#endif


#if defined(PIN_INDICATOR_LED_DIRECTION_A) || defined(PIN_INDICATOR_LED_DIRECTION_B)
#include <arduinosinled.h>
#endif


#ifdef PIN_INDICATOR_LED_DIRECTION_A
fds::SinLed indleda(PIN_INDICATOR_LED_DIRECTION_A);
#endif


#ifdef PIN_INDICATOR_LED_DIRECTION_B
fds::SinLed indledb(PIN_INDICATOR_LED_DIRECTION_B);
#endif


uint8_t b;


void setup() {


#ifdef PIN_INDICATOR_LED_DIRECTION_A
  indleda.initialize(0);
  indleda.fullcycle();
#endif


#ifdef PIN_INDICATOR_LED_DIRECTION_B
  indledb.initialize(0);
  indledb.fullcycle();
#endif


  Serial.begin(BAUD_RATE);
  while (!Serial) { ; /* wait for serial USB-port to connect */ }


  // set the data rate for the SoftwareSerial port connected to the TTL to RS-485 module
  softser.begin(BAUD_RATE);


#ifdef USING_MAX_485
#ifdef RS485_MASTER
  max485.initialize(Rs485Role::Master);
#else
  // set Slave-Mode (not really necessary since this is the default library configuration)
  max485.initialize(Rs485Role::Slave);
#endif
  max485.sending(issending);
#endif
}


void loop() {
#ifdef SEND_ALL_BUFFERED
  while (Serial.available()) {
#else
  if (Serial.available()) {
#endif
#ifdef USING_MAX_485
    if (!issending) {
#ifdef PIN_INDICATOR_LED_DIRECTION_A
      digitalWrite(PIN_INDICATOR_LED_DIRECTION_A, HIGH);
#endif
      issending = true;
      max485.sending(issending);
    }
#endif
    b = Serial.read();
    softser.write(b);
  }
#ifdef USING_MAX_485
  if (issending) {
#ifdef PIN_INDICATOR_LED_DIRECTION_A
    digitalWrite(PIN_INDICATOR_LED_DIRECTION_A, LOW);
#endif
    issending = false;
    max485.sending(issending);
  }
#endif
#ifdef SEND_ALL_BUFFERED
  while (softser.available()) {
#else
  if (altserial.available()) {
#endif
#ifdef PIN_INDICATOR_LED_DIRECTION_B
    if (!isreceiving) {
      digitalWrite(PIN_INDICATOR_LED_DIRECTION_B, HIGH);
      isreceiving = true;
    }
#endif
    b = softser.read();
    Serial.write(b);
  }
#ifdef PIN_INDICATOR_LED_DIRECTION_B
  if (isreceiving) {
    digitalWrite(PIN_INDICATOR_LED_DIRECTION_B, LOW);
    isreceiving = false;
  }
#endif
}

// code stored in the sketch: rs485usbpromicro2.ino
/*
 * Name:    rs485usb.ino
 * Created: 7/14/2019 2:23:09 AM
 * Author:  SigurdssonGO
 * 
 * Software Serial Limitations
 * 
 * The RX pin must support change interrupt
 * On the Mega and Mega 2560 support the following can be used for RX: 10, 11, 12, 13, 14, 15, 50, 51, 52, 53, A8 (62), A9 (63), A10 (64), A11 (65), A12 (66), A13 (67), A14 (68), A15 (69).
 * On the Leonardo and Micro the following can be used for RX: 8, 9, 10, 11, 14 (MISO), 15 (SCK), 16 (MOSI)
 * 
 * On Arduino or Genuino 101 the current maximum RX speed is 57600bps
 * On Arduino or Genuino 101 RX doesn't work on Pin 13
 * 
 */


#include <SoftwareSerial.h>
#include <MAX485.h>


// 4->RE (MAX485 PIN 2), 7->DE (MAX485 PIN 3)
/* Driver Enable set to HIGH to enable transmitting */
//#define PIN_RS485_RE    8
/* Receiver Enable set to LOW to enable receive */
//#define PIN_RS485_DE    9


// Same pin for RE and DE 7->RE (MAX485 PIN 2), 7->DE (MAX485 PIN 3)
#define PIN_RS485_TE    8



// RX(10)->RO (MAX845 PIN 1), TX(11)->DI (MAX845 PIN 4)
#define PIN_SOFT_RX_RO  10
#define PIN_SOFT_TX_DI  11


#define PIN_INDICATOR_LED_DIRECTION_A 5
#define PIN_INDICATOR_LED_DIRECTION_B 6


#define BAUD_RATE     9600


#define SEND_ALL_BUFFERED


SoftwareSerial softser(PIN_SOFT_RX_RO, PIN_SOFT_TX_DI);


#if (defined(PIN_RS485_RE) && defined(PIN_RS485_DE)) || defined(PIN_RS485_TE)
#define USING_MAX_485
#define RS485_MASTER
// Setup max485 Control Input
#ifdef PIN_RS485_TE
MAX485 max485(PIN_RS485_TE);
#else
MAX485 max485(PIN_RS485_RE, PIN_RS485_DE);
#endif
bool issending = false, isreceiving = false;
#endif


#if defined(PIN_INDICATOR_LED_DIRECTION_A) || defined(PIN_INDICATOR_LED_DIRECTION_B)
#include <arduinosinled.h>
#endif


#ifdef PIN_INDICATOR_LED_DIRECTION_A
fds::SinLed indleda(PIN_INDICATOR_LED_DIRECTION_A);
#endif


#ifdef PIN_INDICATOR_LED_DIRECTION_B
fds::SinLed indledb(PIN_INDICATOR_LED_DIRECTION_B);
#endif


uint8_t b;


void setup() {


#ifdef PIN_INDICATOR_LED_DIRECTION_A
  indleda.initialize(0);
  indleda.fullcycle();
#endif


#ifdef PIN_INDICATOR_LED_DIRECTION_B
  indledb.initialize(0);
  indledb.fullcycle();
#endif


  Serial.begin(BAUD_RATE);
  while (!Serial) { ; /* wait for serial USB-port to connect */ }


  // set the data rate for the SoftwareSerial port connected to the TTL to RS-485 module
  softser.begin(BAUD_RATE);


#ifdef USING_MAX_485
#ifdef RS485_MASTER
  max485.initialize(Rs485Role::Master);
#else
  // set Slave-Mode (not really necessary since this is the default library configuration)
  max485.initialize(Rs485Role::Slave);
#endif
  max485.sending(issending);
#endif
}


void loop() {
#ifdef SEND_ALL_BUFFERED
  while (Serial.available()) {
#else
  if (Serial.available()) {
#endif
#ifdef USING_MAX_485
    if (!issending) {
#ifdef PIN_INDICATOR_LED_DIRECTION_A
      digitalWrite(PIN_INDICATOR_LED_DIRECTION_A, HIGH);
#endif
      issending = true;
      max485.sending(issending);
    }
#endif
    b = Serial.read();
    softser.write(b);
  }
#ifdef USING_MAX_485
  if (issending) {
#ifdef PIN_INDICATOR_LED_DIRECTION_A
    digitalWrite(PIN_INDICATOR_LED_DIRECTION_A, LOW);
#endif
    issending = false;
    max485.sending(issending);
  }
#endif
#ifdef SEND_ALL_BUFFERED
  while (softser.available()) {
#else
  if (altserial.available()) {
#endif
#ifdef PIN_INDICATOR_LED_DIRECTION_B
    if (!isreceiving) {
      digitalWrite(PIN_INDICATOR_LED_DIRECTION_B, HIGH);
      isreceiving = true;
    }
#endif
    b = softser.read();
    Serial.write(b);
  }
#ifdef PIN_INDICATOR_LED_DIRECTION_B
  if (isreceiving) {
    digitalWrite(PIN_INDICATOR_LED_DIRECTION_B, LOW);
    isreceiving = false;
  }
#endif
}
